# Fritzing sketch wiring (saved by Fritzing 0.9.3b)

parts:
  Part1 = Arduino Nano (Rev3.0)
  R1 = Resistor [tolerance=±5% resistance=220 package=THT]
  LED1 = LED - 3mm [color="Red (633nm)" package="3 mm [THT]"]
  R2 = Resistor [tolerance=±5% resistance=220 package=THT]
  LED2 = LED - 3mm [color="Red (633nm)" package="3 mm [THT]"]
  S1 = Pushbutton [package="[SMD]"]
  S2 = Pushbutton [package="[SMD]"]
  NRF24L1 = NRF24L01
  R4 = Rotary Potentiometer (Small) [maximum_resistance=100kΩ package=THT]
  C3 = Ceramic Capacitor [capacitance=10nF package="0805 [SMD, multilayer]"]
  C4 = Electrolytic Capacitor [capacitance=1000µF package="300 mil [THT, electrolytic]"]
  S3 = Pushbutton [package="[SMD]"]
  SSR = RELAY-SOLIDSTATE [package=relay-s108t02]  # not connected
  J1a = female pin header, 8 pins [form="♀ (female)"]
  J1b = female pin header, 8 pins [form="♀ (female)"]
  F1 = FUSE [package=fuse_5mm]  # not connected
  JS1 = female pin header, 3 pins [form="♀ (female)"]
  JS2 = female pin header, 3 pins [form="♀ (female)"]
  JS3 = female pin header, 3 pins [form="♀ (female)"]
  J-SSR-1 = female pin header, 2 pins [form="♀ (female)"]
  R3 = Resistor [tolerance=±5% resistance=330 package="0805 [SMD]"]
  J-PSU-5 = female pin header, 2 pins [form="♀ (female)"]
  J-Fuse = rounded female pin header, 2 pins [form="♀ (female rounded)"]
  J220-In = Camdenboss CTB0158-2 [part_number=. package=THT]
  J-SSR-2 = rounded female pin header, 2 pins [form="♀ (female rounded)"]
  J220-Out = Camdenboss CTB0158-2 [part_number=. package=THT]
  J-Earth = Camdenboss CTB0158-2 [part_number=. package=THT]
  J-PSU-220 = rounded female alternating pin header, 3 pins [form="♀ (female rounded)"]

nets (from the breadboard view):
  N1: Part1.RESET, J1a.pin1
  GND: Part1.GND, NRF24L1.GND, C3.0, C4.-, J1a.pin2, JS1.pin1, JS2.pin1, JS3.pin1, J-SSR-1.pin1, J-PSU-5.pin2
  N2: Part1.D5, R1.Pin_1
  N3: Part1.D6, R2.Pin_1
  N4: Part1.D7, J1a.pin5
  N5: Part1.D8, J1a.pin6
  N6: Part1.D9, NRF24L1.CE
  N7: Part1.D10, NRF24L1.CSN
  N8: Part1.D11/MOSI, NRF24L1.MOSI
  N9: Part1.D12/MISO, NRF24L1.MISO
  N10: Part1.5V, C4.+, J1a.pin8, JS1.pin3, JS2.pin3, JS3.pin3, J-PSU-5.pin1
  N11: Part1.A3, R3.Pin_0
  N12: Part1.A2, J-SSR-1.pin2
  N13: Part1.A0, C3.1, J1a.pin7
  3V3: Part1.3V3, NRF24L1.VCC
  N14: Part1.D13/SCK, NRF24L1.SCK
  N15: R1.Pin_0, J1a.pin3
  N16: LED1.cathode, LED2.cathode, S2.Pin_3, S2.Pin_4
  N17: LED1.anode, J1b.pin4
  N18: R2.Pin_0, J1a.pin4
  N19: LED2.anode, J1b.pin3
  N20: S1.Pin_1, S1.Pin_2, J1b.pin6
  N21: S1.Pin_3, S1.Pin_4, R4.leg1, S3.Pin_1, S3.Pin_2, J1b.pin2
  N22: S2.Pin_1, S2.Pin_2, J1b.pin5
  N23: R4.wiper, J1b.pin7
  N24: R4.leg2, J1b.pin8
  N25: S3.Pin_3, J1b.pin1
  N26: JS1.pin2, JS2.pin2, JS3.pin2, R3.Pin_1
  N27: J-Fuse.pin1, J220-In.terminal_1
  N28: J-Fuse.pin2, J-SSR-2.pin1, J-PSU-220.pin1
  N29: J220-In.terminal_2, J220-Out.terminal_1, J-PSU-220.pin2
  N30: J-SSR-2.pin2, J220-Out.terminal_2
  N31: J-Earth.terminal_1, J-Earth.terminal_2, J-PSU-220.pin3

custom parts:
  NRF24L01: NRF24L01 module
